// Logisim project EIPE16.circ as structural Verilog
module EIPE16GP (
  input  SingleCycleFetch,
  input  clk,
  input  [7:0] inst_6,
  input  [7:0] inst_5,
  input  [7:0] inst_4,
  input  [7:0] inst_3,
  input  [7:0] inst_2,
  input  [7:0] inst_1,
  input  useBuiltIn,
  input  reset,
  input  Interrupt,
  input  rAccept,
  input  [15:0] Peripheral1,
  input  [15:0] Peripheral2,
  input  [15:0] Peripheral3,
  input  [15:0] Peripheral4,
  input  [15:0] GA,
  output AcceptClock,
  output RequestJump,
  output RequestWrite,
  output [15:0] WriteValue,
  output [15:0] P1,
  output Pout1,
  output [15:0] P2,
  output Pout2,
  output [15:0] P3,
  output Pout3,
  output [15:0] P4,
  output Pout4,
  output [15:0] GPU,
  output RRQ,
  output ClkOut
);

  wire and_1_out, and_2_out, and_3_out, and_4_out, and_5_out, and_6_out, and_7_out, and_9_out, and_10_out,
       and_11_out, and_12_out, and_13_out, and_14_out, and_15_out, and_16_out, and_17_out, and_18_out,
       and_19_out, and_20_out, and_21_out, and_22_out, and_23_out, and_24_out, and_25_out, and_26_out,
       bitselector_1_out, BR_q, buffer_1_out, buffer_2_out, buffer_3_out, buffer_4_out, buffer_5_out,
       buffer_6_out, buffer_7_out, Bytes_carry, controlled_buffer_1_out, d_ff_1_q, demultiplexer_1_out0,
       demultiplexer_1_out1, demultiplexer_1_out2, demultiplexer_1_out3, demultiplexer_1_out4,
       demultiplexer_1_out5, demultiplexer_1_out8, demultiplexer_1_out9, demultiplexer_1_out10,
       demultiplexer_1_out11, demultiplexer_1_out12, demultiplexer_1_out13, demultiplexer_1_out14,
       demultiplexer_1_out15, demultiplexer_1_out16, demultiplexer_1_out18, demultiplexer_1_out19,
       demultiplexer_1_out20, demultiplexer_1_out21, demultiplexer_1_out22, demultiplexer_1_out23,
       demultiplexer_1_out24, demultiplexer_1_out25, demultiplexer_1_out26, demultiplexer_1_out27,
       demultiplexer_1_out29, demultiplexer_1_out30, demultiplexer_1_out31, demultiplexer_2_out0,
       demultiplexer_2_out1, demultiplexer_2_out2, demultiplexer_3_out0, demultiplexer_3_out1,
       demultiplexer_3_out2, demultiplexer_3_out3, demultiplexer_3_out5, not_1_out, not_2_out, not_3_out,
       not_4_out, not_5_out, not_6_out, not_7_out, not_8_out, or_1_out, or_3_out, or_4_out, or_5_out,
       or_6_out, or_7_out, or_8_out, or_9_out, or_10_out, or_11_out, or_12_out, or_13_out, s_r_ff_1_qn,
       s_r_ff_2_q, s_r_ff_2_qn, s_r_ff_3_q, t_ff_1_q, t_ff_1_qn, The_Tower_out_3;
  wire [1:0] InstructionChip_data;
  wire [4:0] bitselector_2_out, bitselector_4_out, bitselector_5_out, bitselector_6_out, bitselector_7_out,
       bitselector_8_out, bitselector_9_out;
  wire [7:0] adder_2_out, controlled_buffer_3_out, controlled_buffer_4_out, controlled_buffer_5_out,
       controlled_buffer_6_out, controlled_buffer_7_out, controlled_buffer_8_out, controlled_buffer_9_out,
       DebugInst_data, InstructionLUT_data, MicroInstOffset_q, multiplexer_1_out, multiplexer_2_out,
       register_2_q, shift_register_1_q0, shift_register_1_q1;
  wire [7:2] InstructionChip_data_2;
  wire [15:0] ALU_1_carry, ALU_1_out_6, bit_extender_1_out, bitselector_3_out, CARRY_q, counter_1_q,
       counter_2_q, demultiplexer_4_out0, demultiplexer_4_out1, demultiplexer_4_out2, demultiplexer_4_out3,
       demultiplexer_4_out5, demultiplexer_4_out7, multiplexer_3_out, multiplexer_4_out, multiplexer_5_out,
       multiplexer_6_out, multiplexer_7_out, nand_1_out, R1_q, R2_q, R3_q, R4_q, register_1_q, Stack_dout;
  wire [47:0] shift_register_2_q2;

  Register #(.width(16)) register_1 (
    .D(WriteValue), .en(RequestJump), .Q(register_1_q), .clk(RequestJump));  // open: clr
  and and_1 (and_1_out, not_1_out, t_ff_1_qn);
  and and_2 (and_2_out, RequestJump, or_7_out);
  not not_1 (not_1_out, and_2_out);
  buf buffer_1 (buffer_1_out, clk);
  buf buffer_2 (buffer_2_out, buffer_1_out);
  assign controlled_buffer_1_out = reset ? reset : 1'bz;  // Controlled_Buffer controlled_buffer_1
  not not_2 (not_2_out, reset);
  assign controlled_buffer_1_out = not_2_out ? Interrupt : 1'bz;  // Controlled_Buffer controlled_buffer_2
  Counter #(.max('hffff), .trigger("falling"), .width(16)) counter_1 (
    .load(and_2_out), .D(register_1_q), .count(and_1_out), .Q(counter_1_q), .clk(and_3_out), .clr(reset));  // open: carry, up
  and and_3 (and_3_out, clk, s_r_ff_1_qn);
  not not_3 (not_3_out, buffer_2_out);
  ROM #(.addrWidth(16)) DebugInst (.addr(counter_1_q), .data(DebugInst_data));
  S_R_Flip_Flop s_r_ff_1 (
    .S(demultiplexer_1_out22), .clk(not_3_out), .R(controlled_buffer_1_out), .Qn(s_r_ff_1_qn),
    .reset(controlled_buffer_1_out));  // open: Q, preset
  and and_4 (and_4_out, rAccept, SingleCycleFetch);
  not not_4 (not_4_out, SingleCycleFetch);
  and and_5 (and_5_out, not_4_out, rAccept);
  and and_6 (and_6_out, rAccept, or_7_out);
  D_Flip_Flop d_ff_1 (.clk(and_6_out), .D(demultiplexer_1_out18), .Q(d_ff_1_q));  // open: Qn, preset, reset
  and and_7 (and_7_out, d_ff_1_q, and_5_out);
  and and_8 (AcceptClock, t_ff_1_qn, s_r_ff_1_qn);
  S_R_Flip_Flop s_r_ff_2 (
    .clk(or_7_out), .Q(s_r_ff_2_q), .Qn(s_r_ff_2_qn), .preset(demultiplexer_2_out0), .reset(t_ff_1_qn));  // open: S, R
  or or_1 (or_1_out, and_4_out, d_ff_1_q);
  Adder #(.width(16)) adder_1 (.a(bit_extender_1_out), .b(multiplexer_7_out), .out(WriteValue));  // open: cin, cout
  assign bit_extender_1_out = {{15{1'b0}}, and_7_out};  // Bit_Extender bit_extender_1
  and and_9 (and_9_out, demultiplexer_1_out12, bitselector_1_out);
  and and_10 (and_10_out, demultiplexer_1_out11, ~bitselector_1_out);  // AND_Gate
  buf buffer_3 (buffer_3_out, s_r_ff_2_q);
  buf buffer_4 (buffer_4_out, buffer_3_out);
  Shift_Register #(.length(2), .width(8)) shift_register_1 (
    .shift(and_5_out), .in(inst_1), .clk(and_18_out), .load(and_4_out), .clr(and_11_out), .d0(inst_2),
    .q0(shift_register_1_q0), .d1(inst_1), .q1(shift_register_1_q1));  // open: out
  and and_11 (and_11_out, or_7_out, not_5_out);
  not not_5 (not_5_out, demultiplexer_1_out18);
  and and_12 (and_12_out, or_1_out, and_6_out);
  or or_2 (RequestJump, RequestWrite, demultiplexer_1_out21, and_9_out, and_10_out, demultiplexer_1_out20, and_13_out, and_14_out, demultiplexer_1_out13);
  and and_13 (and_13_out, demultiplexer_1_out10, BR_q);
  and and_14 (and_14_out, demultiplexer_1_out9, ~BR_q);  // AND_Gate
  not not_6 (not_6_out, SingleCycleFetch);
  Register register_2 (
    .D(multiplexer_3_out[7:0]), .en(buffer_5_out), .Q(register_2_q), .clk(buffer_5_out));  // open: clr
  buf buffer_5 (buffer_5_out, buffer_4_out);
  Multiplexer #(.width(8)) multiplexer_1 (
    .in0(register_2_q), .in1(InstructionLUT_data), .out(multiplexer_1_out), .sel(s_r_ff_2_qn));
  or or_3 (or_3_out, not_5_out, and_12_out);
  Multiplexer #(.width(8)) multiplexer_2 (
    .in0(inst_1), .in1(DebugInst_data), .out(multiplexer_2_out), .sel(useBuiltIn));
  and and_15 (and_15_out, not_6_out, or_4_out);
  or or_4 (or_4_out, demultiplexer_2_out0, t_ff_1_qn);
  ROM InstructionLUT (.addr(shift_register_2_q2[47:40]), .data(InstructionLUT_data));
  ROM InstructionChip (.addr(adder_2_out), .data({InstructionChip_data_2, InstructionChip_data}));
  Adder adder_2 (.a(multiplexer_1_out), .b(MicroInstOffset_q), .out(adder_2_out));  // open: cin, cout
  S_R_Flip_Flop #(.trigger("falling")) s_r_ff_3 (
    .Q(s_r_ff_3_q), .preset(or_3_out), .reset(demultiplexer_1_out18));  // open: S, clk, R, Qn
  not not_7 (not_7_out, clk);
  assign nand_1_out = ~({16{1'b0}} & CARRY_q);  // NAND_Gate nand_1, 16 bits wide
  BitSelector #(.width(16)) bitselector_1 (.in(nand_1_out), .out(bitselector_1_out), .sel(4'b1111));
  Counter #(.max('h5), .trigger("falling")) Bytes (
    .count(and_15_out), .carry(Bytes_carry), .clk(and_3_out), .clr(and_16_out));  // open: load, D, Q, up
  or or_5 (or_5_out, Bytes_carry, not_8_out);
  and and_16 (and_16_out, and_21_out, ~and_3_out);  // AND_Gate
  and and_17 (and_17_out, InstructionChip_data_2[5], 1'b1);
  Counter #(.ongoal("stay")) MicroInstOffset (
    .count(t_ff_1_q), .Q(MicroInstOffset_q), .clk(and_3_out), .clr(or_4_out));  // open: load, D, carry, up
  and and_18 (and_18_out, rAccept, demultiplexer_1_out18, not_7_out);
  Demultiplexer #(.select(5)) demultiplexer_1 (
    .out0(demultiplexer_1_out0), .out1(demultiplexer_1_out1), .out2(demultiplexer_1_out2),
    .out3(demultiplexer_1_out3), .out4(demultiplexer_1_out4), .out5(demultiplexer_1_out5),
    .out8(demultiplexer_1_out8), .out9(demultiplexer_1_out9), .out10(demultiplexer_1_out10),
    .out11(demultiplexer_1_out11), .out12(demultiplexer_1_out12), .out13(demultiplexer_1_out13),
    .out14(demultiplexer_1_out14), .out15(demultiplexer_1_out15), .out16(demultiplexer_1_out16),
    .out17(RequestWrite), .out18(demultiplexer_1_out18), .out19(demultiplexer_1_out19),
    .out20(demultiplexer_1_out20), .out21(demultiplexer_1_out21), .out22(demultiplexer_1_out22),
    .out23(demultiplexer_1_out23), .out24(demultiplexer_1_out24), .out25(demultiplexer_1_out25),
    .out26(demultiplexer_1_out26), .out27(demultiplexer_1_out27), .out29(demultiplexer_1_out29),
    .out30(demultiplexer_1_out30), .out31(demultiplexer_1_out31), .in(1'b1), .sel(bitselector_2_out));  // open: out6, out7, out28
  BitSelector #(.group(5)) bitselector_2 (
    .in({InstructionChip_data_2, InstructionChip_data}), .out(bitselector_2_out), .sel(1'b0));
  Demultiplexer #(.select(2)) demultiplexer_2 (
    .out0(demultiplexer_2_out0), .out1(demultiplexer_2_out1), .out2(demultiplexer_2_out2), .in(and_17_out),
    .sel(InstructionChip_data));  // open: out3
  buf buffer_6 (buffer_6_out, not_8_out);
  buf buffer_7 (buffer_7_out, buffer_6_out);
  and and_19 (and_19_out, and_3_out, buffer_7_out);
  not not_8 (not_8_out, not_6_out);
  assign controlled_buffer_3_out = and_20_out ? multiplexer_2_out : 8'bz;  // Controlled_Buffer controlled_buffer_3
  and and_20 (and_20_out, not_6_out, t_ff_1_qn);
  // Probe on shift_register_2_q2
  T_Flip_Flop #(.trigger("falling")) t_ff_1 (
    .clk(or_7_out), .Q(t_ff_1_q), .Qn(t_ff_1_qn), .preset(demultiplexer_2_out2), .reset(and_21_out));  // open: T
  and and_21 (and_21_out, demultiplexer_2_out1, and_3_out);
  assign controlled_buffer_4_out = not_8_out ? inst_3 : 8'bz;  // Controlled_Buffer controlled_buffer_4
  assign controlled_buffer_5_out = not_8_out ? inst_4 : 8'bz;  // Controlled_Buffer controlled_buffer_5
  assign controlled_buffer_6_out = not_8_out ? inst_5 : 8'bz;  // Controlled_Buffer controlled_buffer_6
  assign controlled_buffer_7_out = not_8_out ? inst_6 : 8'bz;  // Controlled_Buffer controlled_buffer_7
  Shift_Register #(.length(6), .width(8)) shift_register_2 (
    .shift(and_20_out), .in(controlled_buffer_3_out), .clk(or_6_out), .out(shift_register_2_q2[47:40]),
    .load(not_8_out), .clr(reset), .d0(controlled_buffer_7_out), .q0(shift_register_2_q2[7:0]),
    .d1(controlled_buffer_6_out), .q1(shift_register_2_q2[15:8]), .d2(controlled_buffer_5_out),
    .q2(shift_register_2_q2[23:16]), .d3(controlled_buffer_4_out), .q3(shift_register_2_q2[31:24]),
    .d4(controlled_buffer_9_out), .q4(shift_register_2_q2[39:32]), .d5(controlled_buffer_8_out));  // open: q5
  or or_6 (or_6_out, and_19_out, and_3_out);
  assign controlled_buffer_8_out = not_8_out ? multiplexer_2_out : 8'bz;  // Controlled_Buffer controlled_buffer_8
  assign controlled_buffer_9_out = not_8_out ? inst_2 : 8'bz;  // Controlled_Buffer controlled_buffer_9
  and and_22 (and_22_out, or_5_out, and_3_out);
  and and_23 (and_23_out, s_r_ff_3_q, and_22_out);
  or or_7 (or_7_out, and_23_out, and_18_out);
  BitSelector #(.group(16), .width(1)) bitselector_3 (.in(BR_q), .out(bitselector_3_out), .sel(1'b0));
  delayer The_Tower (.in_1(or_7_out), .in_2(3'b101), .out_3(The_Tower_out_3));
  Multiplexer #(.select(5), .width(16)) multiplexer_3 (
    .in0(R1_q), .in1(R2_q), .in2(R3_q), .in3(R4_q), .in4(CARRY_q), .in5(bitselector_3_out), .in6(GA),
    .in7(Peripheral1), .in8(Peripheral2), .in9(Peripheral3), .in10(Peripheral4), .in11(counter_2_q),
    .in18(shift_register_2_q2[15:0]), .out(multiplexer_3_out), .sel(bitselector_4_out));  // open: in12, in13, in14, in15, in16, in17, in19, in20, in21, in22, in23, in24, in25, in26, in27, in28, in29, in30, in31
  BitSelector #(.group(5)) bitselector_4 (.in(shift_register_2_q2[39:32]), .out(bitselector_4_out), .sel(1'b0));
  Multiplexer #(.select(5), .width(16)) multiplexer_4 (
    .in0(R1_q), .in1(R2_q), .in2(R3_q), .in3(R4_q), .in4(CARRY_q), .in6(GA), .in7(Peripheral1),
    .in8(Peripheral2), .in9(Peripheral3), .in10(Peripheral4), .in11(counter_2_q),
    .in18(shift_register_2_q2[15:0]), .out(multiplexer_4_out), .sel(bitselector_5_out));  // open: in5, in12, in13, in14, in15, in16, in17, in19, in20, in21, in22, in23, in24, in25, in26, in27, in28, in29, in30, in31
  BitSelector #(.group(5)) bitselector_5 (.in(shift_register_2_q2[31:24]), .out(bitselector_5_out), .sel(1'b0));
  or or_8 (or_8_out, demultiplexer_1_out0, demultiplexer_1_out1, demultiplexer_1_out2, demultiplexer_1_out3, demultiplexer_1_out4, demultiplexer_1_out5, demultiplexer_1_out8, demultiplexer_1_out14, demultiplexer_1_out15, demultiplexer_1_out16, demultiplexer_1_out18, demultiplexer_1_out19, demultiplexer_1_out24, demultiplexer_1_out25, demultiplexer_1_out26, demultiplexer_1_out27, demultiplexer_1_out29, demultiplexer_1_out30, demultiplexer_1_out31);
  Register #(.width(16)) R1 (
    .D(demultiplexer_4_out0), .en(demultiplexer_3_out0), .Q(R1_q), .clk(The_Tower_out_3), .clr(reset));
  BitSelector #(.group(5)) bitselector_6 (
    .in({InstructionChip_data_2, InstructionChip_data}), .out(bitselector_6_out), .sel(1'b0));
  Demultiplexer #(.select(5)) demultiplexer_3 (
    .out0(demultiplexer_3_out0), .out1(demultiplexer_3_out1), .out2(demultiplexer_3_out2),
    .out3(demultiplexer_3_out3), .out5(demultiplexer_3_out5), .out7(Pout1), .out8(Pout2), .out9(Pout3),
    .out10(Pout4), .in(or_8_out), .sel(bitselector_7_out));  // open: out4, out6, out11, out12, out13, out14, out15, out16, out17, out18, out19, out20, out21, out22, out23, out24, out25, out26, out27, out28, out29, out30, out31
  BitSelector #(.group(5)) bitselector_7 (.in(shift_register_2_q2[23:16]), .out(bitselector_7_out), .sel(1'b0));
  Register #(.width(16)) R2 (
    .D(demultiplexer_4_out1), .en(demultiplexer_3_out1), .Q(R2_q), .clk(The_Tower_out_3), .clr(reset));
  and and_24 (and_24_out, or_7_out, or_13_out);
  Register #(.width(16)) R3 (
    .D(demultiplexer_4_out2), .en(demultiplexer_3_out2), .Q(R3_q), .clk(The_Tower_out_3), .clr(reset));
  ALU ALU_1 (
    .CR(CARRY_q), .ClkIn(or_7_out), .Operand1(multiplexer_3_out), .Operand2(multiplexer_4_out),
    .Inst(bitselector_6_out), .out_6(ALU_1_out_6), .Carry(ALU_1_carry));
  or or_9 (or_9_out, and_24_out, and_25_out);
  and and_25 (and_25_out, or_11_out, and_26_out);
  Register #(.width(16)) R4 (
    .D(demultiplexer_4_out3), .en(demultiplexer_3_out3), .Q(R4_q), .clk(The_Tower_out_3), .clr(reset));
  Multiplexer #(.width(16)) multiplexer_5 (
    .in0(multiplexer_3_out), .in1(Stack_dout), .out(multiplexer_5_out), .sel(demultiplexer_1_out21));
  or or_10 (or_10_out, or_11_out, or_13_out);
  or or_11 (or_11_out, demultiplexer_2_out1, demultiplexer_1_out20);
  or or_12 (or_12_out, demultiplexer_1_out23, demultiplexer_1_out3, demultiplexer_1_out0, demultiplexer_1_out4);
  Register #(.width(16)) CARRY (.D(ALU_1_carry), .en(or_12_out), .Q(CARRY_q), .clk(The_Tower_out_3), .clr(reset));
  Counter #(.max('hffff), .width(16)) counter_2 (
    .count(or_10_out), .Q(counter_2_q), .up(or_11_out), .clk(or_9_out));  // open: load, D, carry, clr
  RAM #(.addrWidth(16), .dataWidth(16), .enables("line")) Stack (
    .addr(counter_2_q), .we(or_11_out), .clk(and_26_out), .din(multiplexer_3_out), .dout(Stack_dout));
  and and_26 (and_26_out, or_7_out, or_10_out);
  or or_13 (or_13_out, demultiplexer_1_out21, demultiplexer_1_out8);
  Register #(.width(1)) BR (
    .D(demultiplexer_4_out5[0]), .en(demultiplexer_3_out5), .Q(BR_q), .clk(The_Tower_out_3), .clr(reset));
  Demultiplexer #(.select(5), .width(16)) demultiplexer_4 (
    .out0(demultiplexer_4_out0), .out1(demultiplexer_4_out1), .out2(demultiplexer_4_out2),
    .out3(demultiplexer_4_out3), .out5(demultiplexer_4_out5), .out6(GPU), .out7(demultiplexer_4_out7),
    .out8(P2), .out9(P3), .out10(P4), .in(multiplexer_6_out), .sel(bitselector_9_out));  // open: out4, out11, out12, out13, out14, out15, out16, out17, out18, out19, out20, out21, out22, out23, out24, out25, out26, out27, out28, out29, out30, out31
  Multiplexer #(.select(5), .width(16)) multiplexer_6 (
    .in0(ALU_1_out_6), .in1(ALU_1_out_6), .in2(ALU_1_out_6), .in3(ALU_1_out_6), .in8(Stack_dout),
    .in14(ALU_1_out_6), .in15(ALU_1_out_6), .in16(ALU_1_out_6),
    .in18({shift_register_1_q0, shift_register_1_q1}), .in19(multiplexer_3_out), .in23(ALU_1_out_6),
    .in24(ALU_1_out_6), .in25(ALU_1_out_6), .in26(ALU_1_out_6), .out(multiplexer_6_out),
    .sel(bitselector_8_out));  // open: in4, in5, in6, in7, in9, in10, in11, in12, in13, in17, in20, in21, in22, in27, in28, in29, in30, in31
  BitSelector #(.group(5)) bitselector_8 (
    .in({InstructionChip_data_2, InstructionChip_data}), .out(bitselector_8_out), .sel(1'b0));
  BitSelector #(.group(5)) bitselector_9 (.in(shift_register_2_q2[23:16]), .out(bitselector_9_out), .sel(1'b0));
  assign P1 = demultiplexer_4_out7;  // Buffer buffer_8, 16 bits wide
  Multiplexer #(.width(16)) multiplexer_7 (
    .in0(multiplexer_5_out), .in1(multiplexer_4_out), .out(multiplexer_7_out), .sel(RequestWrite));
  and and_27 (RRQ, demultiplexer_1_out18, clk);
  and and_28 (ClkOut, clk, The_Tower_out_3);

  // Notes on the sheet:
  //   EIPE 16 GP
  //   8 bit inst
  //   8 bit operand 1
  //   8 bit operand 2
  //   8 bit output
  //   16 bit imm
  //   contents of DebugInst (hex, n*v repeats v):
  //   12 12 4*0 13 8 4*0 1a 0 12 5 0 7 a 12 0 0 0 1e d 12 0 0 0 6 13 12 0 8 0 0 e 0 12 7 0 7f 13 12 4*0 d
  //   12 0 0 0 6
  //   Debug, can be removed
  //   contents of InstructionLUT (hex, n*v repeats v):
  //   0 1 2 3 4 5 6 7 8 9 a b c d e f 10 11 16 17 18 19 1a 1b 1c 1d 1e 1f 24 25 26
  //   contents of InstructionChip (hex, n*v repeats v):
  //   0 1 2 3 4 5 6 7 8 9 a b c d e f 10 22 14 11 15 21 12 13 14 15 16 17 18 19 1a 1b 1c 20 21 22 1d 1e 1f
  //   Branching Handler
  //   Of doom, some would say
endmodule

module Motherboard (
);

  wire and_1_out, and_2_out, and_3_out, and_4_out, and_5_out, and_6_out, and_7_out, and_8_out, and_9_out,
       buffer_1_out, buffer_2_out, clock_1_out, comparator_1_eq, comparator_1_gt, CPU_acceptclock,
       CPU_clkout, CPU_pout1, CPU_pout2, CPU_pout3, CPU_requestjump, CPU_requestwrite, CPU_rrq,
       MemMod1_clkout, MMU_1_clkpassthrough, MMU_1_romfilling, MMU_1_wen1, MMU_1_wen2, MMU_1_wen3,
       MMU_1_wen4, MMU_1_wen5, MMU_1_wen6, not_1_out, not_2_out, not_3_out, or_1_out, or_2_out, or_3_out,
       or_4_out, Power_out, Reset_out, rgb_video_1_p1, Run_out, t_ff_1_q, t_ff_2_q, t_ff_2_qn, t_ff_3_q,
       t_ff_3_qn;
  wire [6:0] keyboard_1_data;
  wire [7:0] EEPROM_data, MemMod1_dout1, MemMod1_dout2, MemMod1_dout3, MemMod1_dout4, MemMod1_dout5,
       MemMod1_dout6, MMU_1_a1, MMU_1_a2, MMU_1_a3, MMU_1_a4, MMU_1_a5, MMU_1_a6, MMU_1_dout1, MMU_1_dout2,
       MMU_1_dout3, MMU_1_dout4, MMU_1_dout5, MMU_1_dout6;
  wire [7:7] keyboard_1_avail;
  wire [15:0] adder_1_out, bit_extender_1_out, CPU_p1, CPU_p3, CPU_writevalue, demultiplexer_1_out0,
       demultiplexer_1_out1, MMU_1_roma, multiplexer_1_out, register_1_q, register_2_q, register_3_q;

  ROM #(.addrWidth(16)) EEPROM (.addr(MMU_1_roma), .data(EEPROM_data));
  Button Power (.out(Power_out));
  Button Reset (.out(Reset_out));
  Button Run (.out(Run_out));
  Clock clock_1 (.out(clock_1_out));
  T_Flip_Flop t_ff_1 (.Q(t_ff_1_q), .preset(Run_out));  // open: clk, T, Qn, reset
  T_Flip_Flop t_ff_2 (.clk(Power_out), .T(Power_out), .Q(t_ff_2_q), .Qn(t_ff_2_qn));  // open: preset, reset
  assign bit_extender_1_out = {{12{1'b0}}, 4'b0110};  // Bit_Extender bit_extender_1
  and and_1 (and_1_out, clock_1_out, t_ff_2_qn);
  or or_1 (or_1_out, t_ff_2_q, Reset_out);
  Adder #(.width(16)) adder_1 (.a(register_2_q), .b(bit_extender_1_out), .out(adder_1_out));  // open: cin, cout
  Multiplexer #(.width(16)) multiplexer_1 (
    .in0(adder_1_out), .in1(CPU_writevalue), .out(multiplexer_1_out), .sel(CPU_requestjump));
  Register #(.width(16)) register_1 (
    .D(multiplexer_1_out), .en(or_2_out), .Q(register_1_q), .clk(and_2_out));  // open: clr
  and and_2 (and_2_out, CPU_clkout, CPU_acceptclock);
  Register #(.trigger("falling"), .width(16)) register_2 (
    .D(register_1_q), .en(or_2_out), .Q(register_2_q), .clk(and_1_out), .clr(or_1_out));
  or or_2 (or_2_out, CPU_requestjump, CPU_acceptclock);
  buf buffer_1 (buffer_1_out, and_1_out);
  buf buffer_2 (buffer_2_out, buffer_1_out);
  MemoryModule MemMod1 (
    .aIn1(MMU_1_a1), .dIn1(MMU_1_dout1), .aIn2(MMU_1_a2), .dIn2(MMU_1_dout2), .aIn3(MMU_1_a3),
    .dIn3(MMU_1_dout3), .aIn4(MMU_1_a4), .dIn4(MMU_1_dout4), .aIn5(MMU_1_a5), .dIn5(MMU_1_dout5),
    .aIn6(MMU_1_a6), .dIn6(MMU_1_dout6), .clk(or_3_out), .wIn1(MMU_1_wen1), .wIn2(MMU_1_wen2),
    .wIn3(MMU_1_wen3), .wIn4(MMU_1_wen4), .wIn5(MMU_1_wen5), .wIn6(MMU_1_wen6), .dOut1(MemMod1_dout1),
    .dOut2(MemMod1_dout2), .dOut3(MemMod1_dout3), .dOut4(MemMod1_dout4), .dOut5(MemMod1_dout5),
    .dOut6(MemMod1_dout6), .clkOut(MemMod1_clkout));
  and and_3 (and_3_out, CPU_rrq, MemMod1_clkout);
  or or_3 (or_3_out, and_4_out, and_5_out, and_6_out);
  MemoryManager MMU_1 (
    .Address(register_2_q), .WriteRq(CPU_requestwrite), .Data(CPU_writevalue), .Channels(4'b0110),
    .CDI1(MemMod1_dout1), .CDI2(MemMod1_dout2), .CDI3(MemMod1_dout3), .CDI4(MemMod1_dout4),
    .CDI5(MemMod1_dout5), .CDI6(MemMod1_dout6), .dROM(EEPROM_data), .RomSize(16'h7), .eROM(1'b1),
    .Clk(buffer_2_out), .ReadRq(CPU_rrq), .A1(MMU_1_a1), .A2(MMU_1_a2), .A3(MMU_1_a3), .A4(MMU_1_a4),
    .A5(MMU_1_a5), .A6(MMU_1_a6), .dOut1(MMU_1_dout1), .wEn1(MMU_1_wen1), .dOut2(MMU_1_dout2),
    .wEn2(MMU_1_wen2), .dOut3(MMU_1_dout3), .wEn3(MMU_1_wen3), .dOut4(MMU_1_dout4), .wEn4(MMU_1_wen4),
    .dOut5(MMU_1_dout5), .wEn5(MMU_1_wen5), .dOut6(MMU_1_dout6), .wEn6(MMU_1_wen6), .ROMA(MMU_1_roma),
    .RomFilling(MMU_1_romfilling), .ClkPassthrough(MMU_1_clkpassthrough));
  not not_1 (not_1_out, CPU_acceptclock);
  and and_4 (and_4_out, not_1_out, and_8_out);
  and and_5 (and_5_out, CPU_clkout, not_2_out);
  and and_6 (and_6_out, MMU_1_romfilling, buffer_2_out);
  Comparator #(.mode("unsigned"), .width(4)) comparator_1 (
    .a(4'b0110), .b(4'b0110), .gt(comparator_1_gt), .eq(comparator_1_eq));  // open: lt
  not not_2 (not_2_out, CPU_rrq);
  or or_4 (or_4_out, comparator_1_gt, comparator_1_eq);
  and and_7 (and_7_out, or_4_out, not_3_out);
  and and_8 (and_8_out, MMU_1_clkpassthrough, t_ff_1_q);
  not not_3 (not_3_out, 1'b0);
  EIPE16GP CPU (
    .SingleCycleFetch(and_7_out), .clk(and_8_out), .inst_6(MMU_1_dout6), .inst_5(MMU_1_dout5),
    .inst_4(MMU_1_dout4), .inst_3(MMU_1_dout3), .inst_2(MMU_1_dout2), .inst_1(MMU_1_dout1),
    .useBuiltIn(1'b0), .reset(or_1_out), .rAccept(and_3_out),
    .Peripheral2({{8{1'b0}}, keyboard_1_avail[7], keyboard_1_data}), .P1(CPU_p1), .Pout1(CPU_pout1),
    .Pout2(CPU_pout2), .P3(CPU_p3), .Pout3(CPU_pout3), .RRQ(CPU_rrq), .ClkOut(CPU_clkout),
    .RequestJump(CPU_requestjump), .RequestWrite(CPU_requestwrite), .WriteValue(CPU_writevalue),
    .AcceptClock(CPU_acceptclock));  // open: Interrupt, Peripheral4, GA, Peripheral1, Peripheral3, P2, P4, Pout4, GPU
  TTY #(.cols(48), .rows(12)) tty_1 (.data(CPU_p1[6:0]), .clk(CPU_clkout), .we(CPU_pout1), .clr(and_9_out));
  Keyboard keyboard_1 (
    .clk(CPU_clkout), .re(CPU_pout2), .avail(keyboard_1_avail[7]), .data(keyboard_1_data));  // open: clr
  and and_9 (and_9_out, CPU_clkout, CPU_p1[7]);
  Demultiplexer #(.width(16)) demultiplexer_1 (
    .out0(demultiplexer_1_out0), .out1(demultiplexer_1_out1), .in(CPU_p3), .sel(t_ff_3_q));
  T_Flip_Flop t_ff_3 (.clk(CPU_clkout), .T(CPU_pout3), .Q(t_ff_3_q), .Qn(t_ff_3_qn));  // open: preset, reset
  Register #(.width(16)) register_3 (
    .D(demultiplexer_1_out0), .en(t_ff_3_qn), .Q(register_3_q), .clk(CPU_pout3));  // open: clr
  // RGB_Video #(.cursor("No Cursor"), .height(256), .scale(1), .width(256)) rgb_video_1: pin names not known; wires that end beside it: rgb_video_1_p1, rgb_video_1_p1, register_3_q[15:8], register_3_q[7:0], demultiplexer_1_out1
  and and_10 (rgb_video_1_p1, CPU_clkout, CPU_pout3, t_ff_3_q);

  // Notes on the sheet:
  //   contents of EEPROM (hex, n*v repeats v):
  //   12 12 0 0 0 6 ff
endmodule

// Memory Manager
module MemoryManager (
  input  [15:0] Address,
  input  WriteRq,
  input  [15:0] Data,
  input  [3:0] Channels,
  input  [7:0] CDI1,
  input  [7:0] CDI2,
  input  [7:0] CDI3,
  input  [7:0] CDI4,
  input  [7:0] CDI5,
  input  [7:0] CDI6,
  input  [7:0] dROM,
  input  [15:0] RomSize,
  input  eROM,
  input  Clk,
  input  ReadRq,
  output [7:0] A1,
  output [7:0] A2,
  output [7:0] A3,
  output [7:0] A4,
  output [7:0] A5,
  output [7:0] A6,
  output [7:0] dOut1,
  output wEn1,
  output [7:0] dOut2,
  output wEn2,
  output [7:0] dOut3,
  output wEn3,
  output [7:0] dOut4,
  output wEn4,
  output [7:0] dOut5,
  output wEn5,
  output [7:0] dOut6,
  output wEn6,
  output [15:0] ROMA,
  output RomFilling,
  output ClkPassthrough
);

  wire and_2_out, and_3_out, buffer_1_out, buffer_2_out, buffer_3_out, buffer_4_out, buffer_5_out,
       buffer_6_out, buffer_7_out, comparator_1_eq, comparator_1_lt, comparator_2_gt, comparator_3_gt,
       comparator_4_gt, comparator_5_gt, comparator_6_gt, comparator_7_gt, LdA_carry, not_1_out, not_2_out,
       or_1_out, or_2_out, or_3_out;
  wire [5:0] bit_extender_3_out, multiplier_1_out;
  wire [7:0] adder_1_out, bit_extender_2_out, bitselector_1_out, multiplexer_3_out;
  wire [15:0] bit_extender_1_out, divider_1_out, divider_1_rem, multiplexer_1_out, multiplexer_2_out;
  wire [47:0] shifter_1_out;

  Multiplexer #(.width(16)) multiplexer_1 (.in0(Address), .in1(Data), .out(multiplexer_1_out), .sel(ReadRq));
  assign bit_extender_1_out = {{12{1'b0}}, Channels};  // Bit_Extender bit_extender_1
  Multiplexer #(.width(16)) multiplexer_2 (
    .in0(multiplexer_1_out), .in1(ROMA), .out(multiplexer_2_out), .sel(RomFilling));
  or or_1 (or_1_out, WriteRq, RomFilling);
  Bit_Extender #(.in_width(16), .out_width(8), .\type ("zero")) bit_extender_2 (.in(Data), .out(bit_extender_2_out));
  not not_1 (not_1_out, or_2_out);
  Comparator #(.mode("unsigned"), .width(16)) comparator_1 (
    .a(RomSize), .b(ROMA), .eq(comparator_1_eq), .lt(comparator_1_lt));  // open: gt
  Multiplexer #(.width(8)) multiplexer_3 (
    .in0(bit_extender_2_out), .in1(dROM), .out(multiplexer_3_out), .sel(RomFilling));
  Divider #(.width(16)) divider_1 (
    .a(multiplexer_2_out), .b(bit_extender_1_out), .out(divider_1_out), .rem(divider_1_rem));  // open: upper
  Multiplier #(.width(6)) multiplier_1 (
    .a(bit_extender_3_out), .b(6'b001000), .out(multiplier_1_out));  // open: cin, cout
  Counter #(.max('hffff), .trigger("falling"), .width(16)) LdA (
    .count(or_3_out), .Q(ROMA), .carry(LdA_carry), .clk(Clk));  // open: load, D, up, clr
  and and_1 (RomFilling, eROM, not_1_out);
  or or_2 (or_2_out, LdA_carry, comparator_1_eq);
  or or_3 (or_3_out, RomFilling, comparator_1_lt);
  assign bit_extender_3_out = {{3{1'b0}}, divider_1_rem[2:0]};  // Bit_Extender bit_extender_3
  Shifter #(.shift("rr"), .width(48)) shifter_1 (
    .in({CDI6, CDI5, CDI4, CDI3, CDI2, CDI1}), .\dist (multiplier_1_out), .out(shifter_1_out));
  // Probe on shifter_1_out
  buf buffer_1 (buffer_1_out, Clk);
  buf buffer_2 (buffer_2_out, buffer_1_out);
  not not_2 (not_2_out, or_3_out);
  BitSelector #(.group(8), .width(16)) bitselector_1 (.in(divider_1_out), .out(bitselector_1_out), .sel(1'b0));
  and and_2 (and_2_out, or_1_out, buffer_4_out);
  buf buffer_3 (buffer_3_out, buffer_2_out);
  buf buffer_4 (buffer_4_out, buffer_3_out);
  and and_3 (and_3_out, not_2_out, Clk);
  buf buffer_5 (buffer_5_out, and_3_out);
  buf buffer_6 (buffer_6_out, buffer_5_out);
  // Probe on bitselector_1_out
  // Probe on divider_1_rem[2:0]
  Decoder #(.select(3)) decoder_1 (
    .out0(wEn1), .out1(wEn2), .out2(wEn3), .out3(wEn4), .out4(wEn5), .out5(wEn6), .sel(divider_1_rem[2:0]),
    .en(and_2_out));  // open: out6, out7
  buf buffer_7 (buffer_7_out, buffer_6_out);
  buf buffer_8 (ClkPassthrough, buffer_7_out);
  Adder adder_1 (.a(bitselector_1_out), .b(8'h1), .out(adder_1_out));  // open: cin, cout
  Comparator #(.mode("unsigned"), .width(3)) comparator_2 (
    .a(divider_1_rem[2:0]), .b(3'b000), .gt(comparator_2_gt));  // open: eq, lt
  Comparator #(.mode("unsigned"), .width(3)) comparator_3 (
    .a(divider_1_rem[2:0]), .b(3'b001), .gt(comparator_3_gt));  // open: eq, lt
  Comparator #(.mode("unsigned"), .width(3)) comparator_4 (
    .a(divider_1_rem[2:0]), .b(3'b010), .gt(comparator_4_gt));  // open: eq, lt
  Comparator #(.mode("unsigned"), .width(3)) comparator_5 (
    .a(divider_1_rem[2:0]), .b(3'b011), .gt(comparator_5_gt));  // open: eq, lt
  Comparator #(.mode("unsigned"), .width(3)) comparator_6 (
    .a(divider_1_rem[2:0]), .b(3'b100), .gt(comparator_6_gt));  // open: eq, lt
  Comparator #(.mode("unsigned"), .width(3)) comparator_7 (
    .a(divider_1_rem[2:0]), .b(3'b101), .gt(comparator_7_gt));  // open: eq, lt
  Multiplexer #(.width(8)) multiplexer_4 (.in0(shifter_1_out[47:40]), .in1(multiplexer_3_out), .out(dOut6), .sel(wEn6));
  Multiplexer #(.width(8)) multiplexer_5 (.in0(shifter_1_out[31:24]), .in1(multiplexer_3_out), .out(dOut4), .sel(wEn4));
  Multiplexer #(.width(8)) multiplexer_6 (.in0(shifter_1_out[39:32]), .in1(multiplexer_3_out), .out(dOut5), .sel(wEn5));
  Multiplexer #(.width(8)) multiplexer_7 (.in0(bitselector_1_out), .in1(adder_1_out), .out(A1), .sel(comparator_2_gt));
  Multiplexer #(.width(8)) multiplexer_8 (.in0(bitselector_1_out), .in1(adder_1_out), .out(A2), .sel(comparator_3_gt));
  Multiplexer #(.width(8)) multiplexer_9 (.in0(bitselector_1_out), .in1(adder_1_out), .out(A3), .sel(comparator_4_gt));
  Multiplexer #(.width(8)) multiplexer_10 (.in0(bitselector_1_out), .in1(adder_1_out), .out(A4), .sel(comparator_5_gt));
  Multiplexer #(.width(8)) multiplexer_11 (.in0(bitselector_1_out), .in1(adder_1_out), .out(A5), .sel(comparator_6_gt));
  Multiplexer #(.width(8)) multiplexer_12 (.in0(bitselector_1_out), .in1(adder_1_out), .out(A6), .sel(comparator_7_gt));
  Multiplexer #(.width(8)) multiplexer_13 (.in0(shifter_1_out[7:0]), .in1(multiplexer_3_out), .out(dOut1), .sel(wEn1));
  Multiplexer #(.width(8)) multiplexer_14 (.in0(shifter_1_out[15:8]), .in1(multiplexer_3_out), .out(dOut2), .sel(wEn2));
  Multiplexer #(.width(8)) multiplexer_15 (
    .in0(shifter_1_out[23:16]), .in1(multiplexer_3_out), .out(dOut3), .sel(wEn3));

  // Notes on the sheet:
  //   TODO:
  //   Add the ability to have values bigger than 16 bits support
endmodule

module ALU (
  input  [15:0] CR,
  input  ClkIn,
  input  [15:0] Operand1,
  input  [15:0] Operand2,
  input  [4:0] Inst,
  output [15:0] out_6,
  output [15:0] Carry
);

  wire adder_1_cout, buffer_1_out, buffer_2_out, comparator_2_gt, not_1_out, subtractor_1_bout;
  wire [0:0] comparator_1_eq, comparator_1_gt, comparator_1_lt;
  wire [15:0] adder_1_out, and_1_out, and_2_out, and_3_out, bit_extender_1_out, bitselector_1_out,
       bitselector_2_out, multiplier_1_cout, multiplier_1_out, nand_1_out, not_2_out, register_1_q,
       shifter_1_out, shifter_2_out, shifter_3_out, shifter_4_out, subtractor_1_out, xor_1_out;

  Register #(.width(16)) register_1 (.D(CR), .en(buffer_1_out), .Q(register_1_q), .clk(buffer_1_out), .clr(not_1_out));
  buf buffer_1 (buffer_1_out, buffer_2_out);
  buf buffer_2 (buffer_2_out, ClkIn);
  not not_1 (not_1_out, ClkIn);
  assign and_1_out = Operand1 & Operand2;  // AND_Gate and_1, 16 bits wide
  Adder #(.width(16)) adder_1 (
    .a(Operand1), .b(Operand2), .out(adder_1_out), .cin(register_1_q[0]), .cout(adder_1_cout));
  Subtractor #(.width(16)) subtractor_1 (
    .a(Operand1), .b(Operand2), .out(subtractor_1_out), .bin(register_1_q[0]), .bout(subtractor_1_bout));
  Comparator #(.mode("unsigned")) comparator_1 (
    .gt(comparator_1_gt[0]), .eq(comparator_1_eq[0]), .lt(comparator_1_lt[0]));  // open: a, b
  assign nand_1_out = ~(Operand1 & Operand2);  // NAND_Gate nand_1, 16 bits wide
  Multiplier #(.width(16)) multiplier_1 (
    .a(Operand1), .b(Operand2), .out(multiplier_1_out), .cin(register_1_q), .cout(multiplier_1_cout));
  assign xor_1_out = Operand1 ^ Operand2;  // XOR_Gate xor_1, 16 bits wide
  Shifter #(.width(16)) shifter_1 (.in(Operand1), .\dist (Operand2[3:0]), .out(shifter_1_out));
  Comparator #(.mode("unsigned"), .width(12)) comparator_2 (
    .a(Operand2[15:4]), .b({12{1'b0}}), .gt(comparator_2_gt));  // open: eq, lt
  Shifter #(.shift("rl"), .width(16)) shifter_2 (.in(Operand1), .\dist (Operand2[3:0]), .out(shifter_2_out));
  Shifter #(.shift("lr"), .width(16)) shifter_3 (.in(Operand1), .\dist (Operand2[3:0]), .out(shifter_3_out));
  assign bit_extender_1_out = {{15{1'b1}}, comparator_2_gt};  // Bit_Extender bit_extender_1
  Shifter #(.shift("rr"), .width(16)) shifter_4 (.in(Operand1), .\dist (Operand2[3:0]), .out(shifter_4_out));
  assign not_2_out = ~bit_extender_1_out;  // NOT_Gate not_2, 16 bits wide
  assign and_2_out = not_2_out & shifter_1_out;  // AND_Gate and_2, 16 bits wide
  assign and_3_out = not_2_out & shifter_3_out;  // AND_Gate and_3, 16 bits wide
  BitSelector #(.group(16), .width(1)) bitselector_1 (.in(adder_1_cout), .out(bitselector_1_out), .sel(1'b0));
  BitSelector #(.group(16), .width(1)) bitselector_2 (.in(subtractor_1_bout), .out(bitselector_2_out), .sel(1'b0));
  Multiplexer #(.select(5), .width(16)) multiplexer_1 (
    .in0(adder_1_out), .in1(adder_1_out), .in2(subtractor_1_out), .in3(subtractor_1_out),
    .in4(multiplier_1_out), .in5(multiplier_1_out), .in14(and_1_out), .in15(nand_1_out), .in16(xor_1_out),
    .in23(and_2_out), .in24(shifter_2_out), .in25(and_3_out), .in26(shifter_4_out),
    .in29({{15{1'b0}}, comparator_1_eq[0]}), .in30({{15{1'b0}}, comparator_1_gt[0]}),
    .in31({{15{1'b0}}, comparator_1_lt[0]}), .out(out_6), .sel(Inst));  // open: in6, in7, in8, in9, in10, in11, in12, in13, in17, in18, in19, in20, in21, in22, in27, in28
  Multiplexer #(.select(5), .width(16)) multiplexer_2 (
    .in0(bitselector_1_out), .in3(bitselector_2_out), .in5(multiplier_1_cout), .in23(bitselector_2_out),
    .out(Carry), .sel(Inst));  // open: in1, in2, in4, in6, in7, in8, in9, in10, in11, in12, in13, in14, in15, in16, in17, in18, in19, in20, in21, in22, in24, in25, in26, in27, in28, in29, in30, in31
endmodule

module RenderCore (
  input  [7:0] Inst,
  input  [7:0] PxPos,
  input  [7:0] PxColor,
  output [7:0] PxColorOut
);
endmodule

module GPU (
  input  [15:0] dIn,
  input  CLK
);

  wire [7:0] Pallete_dout;

  RAM #(.enables("line")) VRAM (.clk(CLK));  // open: addr, we, din, dout
  RAM #(.enables("line")) Pallete (.clk(CLK), .dout(Pallete_dout));  // open: addr, we, din
  RAM #(.enables("line")) Buffer1 (.clk(CLK), .din(Pallete_dout));  // open: addr, we, dout
  RAM #(.enables("line")) Buffer2 (.clk(CLK), .din(Pallete_dout));  // open: addr, we, dout
endmodule

module delayer (
  input  in_1,
  input  [2:0] in_2,
  output out_3
);

  wire buffer_1_out, buffer_2_out, buffer_3_out, buffer_4_out, buffer_5_out, buffer_6_out, buffer_7_out,
       buffer_8_out, buffer_9_out, buffer_10_out, buffer_11_out, buffer_12_out, buffer_13_out, buffer_14_out,
       buffer_15_out, buffer_16_out, buffer_17_out, buffer_18_out, buffer_19_out, buffer_20_out,
       buffer_21_out, buffer_22_out, buffer_23_out, buffer_24_out, buffer_25_out, buffer_26_out,
       buffer_27_out, buffer_28_out, buffer_29_out, buffer_30_out, buffer_31_out, buffer_32_out,
       buffer_33_out, buffer_34_out, buffer_35_out, buffer_36_out, buffer_37_out, buffer_38_out,
       buffer_39_out, buffer_40_out, buffer_41_out, buffer_42_out, buffer_43_out, buffer_44_out,
       buffer_45_out, buffer_46_out, buffer_47_out, buffer_48_out, buffer_49_out, buffer_50_out,
       buffer_51_out, buffer_52_out, buffer_53_out, buffer_54_out, buffer_55_out, buffer_56_out,
       buffer_57_out, buffer_58_out, buffer_59_out, buffer_60_out, buffer_61_out, buffer_62_out,
       buffer_63_out, buffer_64_out, buffer_65_out, buffer_66_out, buffer_67_out, buffer_68_out,
       buffer_69_out, buffer_70_out, buffer_71_out, buffer_72_out, buffer_73_out, buffer_74_out,
       buffer_75_out, buffer_76_out, buffer_77_out, buffer_78_out, buffer_79_out, buffer_80_out,
       buffer_81_out, buffer_82_out, buffer_83_out, buffer_84_out, buffer_85_out, buffer_86_out,
       buffer_87_out, buffer_88_out, buffer_89_out, buffer_90_out, buffer_91_out, buffer_92_out,
       buffer_93_out, buffer_94_out, buffer_95_out, buffer_96_out, buffer_97_out, buffer_98_out,
       buffer_99_out, buffer_100_out, buffer_101_out, buffer_102_out, buffer_103_out, buffer_104_out,
       buffer_105_out, buffer_106_out, buffer_107_out, buffer_108_out, buffer_109_out, buffer_110_out,
       buffer_111_out, buffer_112_out, buffer_113_out, buffer_114_out, buffer_115_out, buffer_116_out,
       buffer_117_out, buffer_118_out, buffer_119_out, buffer_120_out;

  buf buffer_1 (buffer_1_out, buffer_3_out);
  buf buffer_2 (buffer_2_out, buffer_5_out);
  buf buffer_3 (buffer_3_out, buffer_7_out);
  buf buffer_4 (buffer_4_out, buffer_1_out);
  buf buffer_5 (buffer_5_out, buffer_9_out);
  buf buffer_6 (buffer_6_out, buffer_2_out);
  buf buffer_7 (buffer_7_out, buffer_11_out);
  buf buffer_8 (buffer_8_out, buffer_4_out);
  buf buffer_9 (buffer_9_out, buffer_13_out);
  buf buffer_10 (buffer_10_out, buffer_6_out);
  buf buffer_11 (buffer_11_out, buffer_15_out);
  buf buffer_12 (buffer_12_out, buffer_8_out);
  buf buffer_13 (buffer_13_out, buffer_17_out);
  buf buffer_14 (buffer_14_out, buffer_10_out);
  buf buffer_15 (buffer_15_out, buffer_19_out);
  buf buffer_16 (buffer_16_out, buffer_12_out);
  buf buffer_17 (buffer_17_out, buffer_21_out);
  buf buffer_18 (buffer_18_out, buffer_14_out);
  buf buffer_19 (buffer_19_out, buffer_23_out);
  buf buffer_20 (buffer_20_out, buffer_16_out);
  buf buffer_21 (buffer_21_out, buffer_25_out);
  buf buffer_22 (buffer_22_out, buffer_18_out);
  buf buffer_23 (buffer_23_out, buffer_27_out);
  buf buffer_24 (buffer_24_out, buffer_20_out);
  buf buffer_25 (buffer_25_out, buffer_29_out);
  buf buffer_26 (buffer_26_out, buffer_22_out);
  buf buffer_27 (buffer_27_out, buffer_31_out);
  buf buffer_28 (buffer_28_out, buffer_24_out);
  buf buffer_29 (buffer_29_out, buffer_33_out);
  buf buffer_30 (buffer_30_out, buffer_26_out);
  buf buffer_31 (buffer_31_out, buffer_35_out);
  buf buffer_32 (buffer_32_out, buffer_28_out);
  buf buffer_33 (buffer_33_out, buffer_37_out);
  buf buffer_34 (buffer_34_out, buffer_30_out);
  buf buffer_35 (buffer_35_out, buffer_39_out);
  buf buffer_36 (buffer_36_out, buffer_32_out);
  buf buffer_37 (buffer_37_out, buffer_41_out);
  buf buffer_38 (buffer_38_out, buffer_34_out);
  buf buffer_39 (buffer_39_out, buffer_43_out);
  buf buffer_40 (buffer_40_out, buffer_36_out);
  buf buffer_41 (buffer_41_out, buffer_45_out);
  buf buffer_42 (buffer_42_out, buffer_38_out);
  buf buffer_43 (buffer_43_out, buffer_47_out);
  buf buffer_44 (buffer_44_out, buffer_40_out);
  buf buffer_45 (buffer_45_out, buffer_49_out);
  buf buffer_46 (buffer_46_out, buffer_42_out);
  buf buffer_47 (buffer_47_out, buffer_51_out);
  buf buffer_48 (buffer_48_out, buffer_44_out);
  buf buffer_49 (buffer_49_out, buffer_53_out);
  buf buffer_50 (buffer_50_out, buffer_46_out);
  buf buffer_51 (buffer_51_out, buffer_55_out);
  buf buffer_52 (buffer_52_out, buffer_48_out);
  buf buffer_53 (buffer_53_out, buffer_57_out);
  buf buffer_54 (buffer_54_out, buffer_50_out);
  buf buffer_55 (buffer_55_out, buffer_59_out);
  buf buffer_56 (buffer_56_out, buffer_52_out);
  buf buffer_57 (buffer_57_out, buffer_61_out);
  buf buffer_58 (buffer_58_out, buffer_54_out);
  buf buffer_59 (buffer_59_out, buffer_63_out);
  buf buffer_60 (buffer_60_out, buffer_56_out);
  buf buffer_61 (buffer_61_out, buffer_65_out);
  buf buffer_62 (buffer_62_out, buffer_58_out);
  buf buffer_63 (buffer_63_out, buffer_67_out);
  buf buffer_64 (buffer_64_out, buffer_60_out);
  buf buffer_65 (buffer_65_out, buffer_69_out);
  buf buffer_66 (buffer_66_out, buffer_62_out);
  buf buffer_67 (buffer_67_out, buffer_71_out);
  buf buffer_68 (buffer_68_out, buffer_64_out);
  buf buffer_69 (buffer_69_out, buffer_73_out);
  buf buffer_70 (buffer_70_out, buffer_66_out);
  buf buffer_71 (buffer_71_out, buffer_75_out);
  buf buffer_72 (buffer_72_out, buffer_68_out);
  buf buffer_73 (buffer_73_out, buffer_77_out);
  buf buffer_74 (buffer_74_out, buffer_70_out);
  buf buffer_75 (buffer_75_out, in_1);
  buf buffer_76 (buffer_76_out, buffer_72_out);
  buf buffer_77 (buffer_77_out, buffer_79_out);
  buf buffer_78 (buffer_78_out, buffer_74_out);
  buf buffer_79 (buffer_79_out, buffer_76_out);
  buf buffer_80 (buffer_80_out, buffer_78_out);
  buf buffer_81 (buffer_81_out, buffer_82_out);
  buf buffer_82 (buffer_82_out, buffer_84_out);
  buf buffer_83 (buffer_83_out, buffer_81_out);
  buf buffer_84 (buffer_84_out, buffer_86_out);
  buf buffer_85 (buffer_85_out, buffer_83_out);
  buf buffer_86 (buffer_86_out, buffer_88_out);
  buf buffer_87 (buffer_87_out, buffer_85_out);
  buf buffer_88 (buffer_88_out, buffer_90_out);
  buf buffer_89 (buffer_89_out, buffer_87_out);
  buf buffer_90 (buffer_90_out, buffer_92_out);
  buf buffer_91 (buffer_91_out, buffer_89_out);
  buf buffer_92 (buffer_92_out, buffer_94_out);
  buf buffer_93 (buffer_93_out, buffer_91_out);
  buf buffer_94 (buffer_94_out, buffer_96_out);
  buf buffer_95 (buffer_95_out, buffer_93_out);
  buf buffer_96 (buffer_96_out, buffer_98_out);
  buf buffer_97 (buffer_97_out, buffer_95_out);
  buf buffer_98 (buffer_98_out, buffer_100_out);
  buf buffer_99 (buffer_99_out, buffer_97_out);
  buf buffer_100 (buffer_100_out, buffer_102_out);
  buf buffer_101 (buffer_101_out, buffer_99_out);
  buf buffer_102 (buffer_102_out, buffer_104_out);
  buf buffer_103 (buffer_103_out, buffer_101_out);
  buf buffer_104 (buffer_104_out, buffer_106_out);
  buf buffer_105 (buffer_105_out, buffer_103_out);
  buf buffer_106 (buffer_106_out, buffer_108_out);
  buf buffer_107 (buffer_107_out, buffer_105_out);
  buf buffer_108 (buffer_108_out, buffer_110_out);
  buf buffer_109 (buffer_109_out, buffer_107_out);
  buf buffer_110 (buffer_110_out, buffer_112_out);
  buf buffer_111 (buffer_111_out, buffer_109_out);
  buf buffer_112 (buffer_112_out, buffer_114_out);
  buf buffer_113 (buffer_113_out, buffer_111_out);
  buf buffer_114 (buffer_114_out, buffer_116_out);
  buf buffer_115 (buffer_115_out, buffer_113_out);
  buf buffer_116 (buffer_116_out, buffer_118_out);
  buf buffer_117 (buffer_117_out, buffer_115_out);
  buf buffer_118 (buffer_118_out, buffer_80_out);
  buf buffer_119 (buffer_119_out, buffer_117_out);
  buf buffer_120 (buffer_120_out, buffer_119_out);
  Multiplexer #(.select(3)) multiplexer_1 (
    .in0(buffer_1_out), .in1(buffer_79_out), .in2(buffer_2_out), .in3(buffer_80_out), .in4(buffer_81_out),
    .in5(buffer_120_out), .out(out_3), .sel(in_2));  // open: in6, in7

  // Notes on the sheet:
  //   Do not stare directly at the tower
endmodule

module TestingGrounds (
  input  in_1,
  input  [3:0] in_2
);

  wire signaldelayer_1_p3;

  // SignalDelayer signaldelayer_1: pin names not known; wires that end beside it: in_1, in_2, signaldelayer_1_p3
endmodule

module MemoryModule (
  input  [7:0] aIn1,
  input  [7:0] dIn1,
  input  wIn1,
  input  [7:0] aIn2,
  input  [7:0] dIn2,
  input  wIn2,
  input  [7:0] aIn3,
  input  [7:0] dIn3,
  input  wIn3,
  input  [7:0] aIn4,
  input  [7:0] dIn4,
  input  wIn4,
  input  [7:0] aIn5,
  input  [7:0] dIn5,
  input  wIn5,
  input  [7:0] aIn6,
  input  [7:0] dIn6,
  input  wIn6,
  input  clk,
  output [7:0] dOut1,
  output [7:0] dOut2,
  output [7:0] dOut3,
  output [7:0] dOut4,
  output [7:0] dOut5,
  output [7:0] dOut6,
  output clkOut
);

  wire buffer_1_out, buffer_2_out, buffer_3_out, buffer_4_out, buffer_5_out, buffer_6_out, buffer_7_out;

  buf buffer_1 (buffer_1_out, clk);
  RAM #(.enables("line"), .trigger("falling")) RAM_1 (
    .addr(aIn1), .we(wIn1), .clk(buffer_1_out), .din(dIn1), .dout(dOut1));
  RAM #(.enables("line"), .trigger("falling")) RAM_2 (
    .addr(aIn2), .we(wIn2), .clk(buffer_1_out), .din(dIn2), .dout(dOut2));
  RAM #(.enables("line"), .trigger("falling")) RAM_4 (
    .addr(aIn3), .we(wIn3), .clk(buffer_1_out), .din(dIn3), .dout(dOut3));
  RAM #(.enables("line"), .trigger("falling")) RAM_3 (
    .addr(aIn4), .we(wIn4), .clk(buffer_1_out), .din(dIn4), .dout(dOut4));
  RAM #(.enables("line"), .trigger("falling")) RAM_5 (
    .addr(aIn5), .we(wIn5), .clk(buffer_1_out), .din(dIn5), .dout(dOut5));
  RAM #(.enables("line"), .trigger("falling")) RAM_6 (
    .addr(aIn6), .we(wIn6), .clk(buffer_1_out), .din(dIn6), .dout(dOut6));
  buf buffer_2 (buffer_2_out, buffer_5_out);
  buf buffer_3 (buffer_3_out, buffer_2_out);
  buf buffer_4 (buffer_4_out, buffer_1_out);
  buf buffer_5 (buffer_5_out, buffer_4_out);
  buf buffer_6 (buffer_6_out, buffer_3_out);
  buf buffer_7 (buffer_7_out, buffer_6_out);
  not not_1 (clkOut, buffer_7_out);
endmodule

// VHDL entity SignalDelayer, as the project stores it:
--------------------------------------------------------------------------------
-- Project :
-- Signal Delayer
-- File    :
-- SignalDelayer
-- Autor   :
-- Comple (CompleCwaft)
-- Date    :
-- 3/29/26
--
--------------------------------------------------------------------------------
-- Description :
-- Delays a signal from propogating in 250 tick intervals
--
--------------------------------------------------------------------------------

LIBRARY ieee;
USE ieee.std_logic_1164.all;
ENTITY SignalDelayer IS
  PORT (
  ------------------------------------------------------------------------------
  --Insert input ports below
    clock      : IN  std_logic;                    -- input bit example
    val        : IN  std_logic_vector(3 DOWNTO 0); -- input vector example
  ------------------------------------------------------------------------------
  --Insert output ports below
    clockOut  : OUT std_logic                      -- output bit example
  );
END SignalDelayer;

--------------------------------------------------------------------------------
--Complete your VHDL description below
--------------------------------------------------------------------------------

ARCHITECTURE TypeArchitecture OF SignalDelayer IS

BEGIN
    p_Process: PROCESS (clock) BEGIN
        clockOut = clock;
    END PROCESS p_Process;

END TypeArchitecture;
